# Fritzing sketch servo_board (saved by Fritzing 0.7.11b)
stripboards: 1

parts:
  J1 = female pin header, 1 pin [form="♀ (female)"]  # not connected
  J3 = male pin header, 8 pins [form="♂ (male)"]  # not connected
  J2 = male pin header, 8 pins [form="♂ (male)"]
  U1 = atmega168 [package=dip]

nets:
  N1: J2.pin4, U1.GND#21
  N2: J2.pin6, U1.A5
  N3: J2.pin7, U1.A4
  N4: J2.pin8, U1.AVCC
